// Logisim project ejer1.circ as structural Verilog: 1 circuit, main circuit main
module main (
  input  in_1,
  input  in_2,
  input  [3:0] in_3,
  input  [3:0] in_4,
  input  in_5,
  output [3:0] out_6,
  output [3:0] out_7
);

  wire adder_1_cout, and_1_out, and_2_out, or_1_out;
  wire [0:0] or_2_out;

  Hex_Digit_Display hex_digit_display_1 (.value(in_4));  // open: dp
  Hex_Digit_Display hex_digit_display_2 (.value(in_3));  // open: dp
  Adder #(.width(4)) adder_1 (.a(in_3), .b(in_4), .out(out_7), .cin(in_1), .cout(adder_1_cout));
  and and_1 (and_1_out, out_7[1], out_7[3]);
  and and_2 (and_2_out, out_7[2], out_7[3]);
  or or_1 (or_1_out, and_1_out, and_2_out);
  or or_2 (or_2_out[0], or_1_out, adder_1_cout);
  Hex_Digit_Display hex_digit_display_3 (.value({{3{in_2}}, or_2_out[0]}));  // open: dp
  Hex_Digit_Display hex_digit_display_4 (.value(out_6));  // open: dp
  Adder #(.width(4)) adder_2 (.a(out_7), .b({in_5, {2{or_2_out[0]}}, in_5}), .out(out_6));  // open: cin, cout
endmodule
