// Logisim project ejer4.circ as structural Verilog: 1 circuit, main circuit main
module main (
  input  [3:0] in_1,
  output out_2
);

  wire decoder_1_out2, decoder_1_out3, decoder_1_out5, decoder_1_out7, decoder_1_out11, decoder_1_out13;

  Decoder #(.select(4), .enable("false")) decoder_1 (
    .out2(decoder_1_out2), .out3(decoder_1_out3), .out5(decoder_1_out5), .out7(decoder_1_out7),
    .out11(decoder_1_out11), .out13(decoder_1_out13), .sel(in_1));  // open: out0, out1, out4, out6, out8, out9, out10, out12, out14, out15
  or or_1 (out_2, decoder_1_out2, decoder_1_out3, decoder_1_out5, decoder_1_out7, decoder_1_out11, decoder_1_out13);
endmodule
