// Logisim project ejer6.circ as structural Verilog: 1 circuit, main circuit main
module main (
  input  [1:0] A,
  input  [1:0] B,
  input  [1:0] selector
);

  wire [1:0] adder_1_out, adder_2_out, adder_3_out, multiplexer_1_out;
  wire [1:1] adder_1_cout, adder_2_cout;

  Adder #(.width(2)) adder_1 (.a(A), .b(B), .out(adder_1_out), .cin(1'b0), .cout(adder_1_cout[1]));
  Adder #(.width(2)) adder_2 (.a(B), .b(A), .out(adder_2_out), .cin(1'b0), .cout(adder_2_cout[1]));
  // Probe on {adder_1_cout[1], adder_1_out[1]}
  // Probe on A
  // Probe on B
  Adder #(.width(2)) adder_3 (
    .a({1'b0, adder_2_out[0]}), .b({adder_2_cout[1], adder_2_out[1]}), .out(adder_3_out), .cin(1'b0));  // open: cout
  Multiplexer #(.select(2), .width(2), .enable("false")) multiplexer_1 (
    .in0({adder_1_cout[1], adder_1_out[1]}), .in1(A), .in2(B), .in3(adder_3_out), .out(multiplexer_1_out),
    .sel(selector));
  // Probe on adder_3_out
  Hex_Digit_Display hex_digit_display_1 (.value({2'b00, multiplexer_1_out}));  // open: dp
endmodule
