// Logisim project ejer1.circ as structural Verilog: 1 circuit, main circuit main
module main (
  input  R,
  input  S,
  output Q,
  output nQ
);

  wire clock_1_out, nand_1_out, nand_4_out;

  Clock clock_1 (.out(clock_1_out));
  nand nand_1 (nand_1_out, R, clock_1_out);
  nand nand_2 (Q, nand_1_out, nQ);
  nand nand_3 (nQ, Q, nand_4_out);
  nand nand_4 (nand_4_out, clock_1_out, S);
endmodule
