// Logisim project ejer4.circ as structural Verilog: 4 circuits, main circuit main
module main (
  input  [1:0] in_1,
  output cambio,
  output E0,
  output E1,
  output producto
);

  wire _0_q, _1_q, and_1_out, and_2_out, clock_1_out, not_1_out, not_2_out, or_1_out, or_2_out,
       Q_prime_0_q0_2, Q_prime_1_q1_2;

  Clock clock_1 (.out(clock_1_out));
  q1 Q_prime_1 (.Q0(_0_q), .Q1(_1_q), .E1(in_1[1]), .E0(in_1[0]), .q1_2(Q_prime_1_q1_2));
  q0 Q_prime_0 (.Q0(_0_q), .Q1(_1_q), .E1(in_1[1]), .E0(in_1[0]), .q0_2(Q_prime_0_q0_2));
  not not_1 (not_1_out, Q_prime_0_q0_2);
  not not_2 (not_2_out, in_1[1]);
  or or_1 (or_1_out, Q_prime_1_q1_2, in_1[1]);
  and and_1 (and_1_out, not_1_out, in_1[0]);
  or or_2 (or_2_out, and_1_out, and_2_out);
  and and_2 (and_2_out, Q_prime_0_q0_2, not_2_out, in_1[0]);
  J_K_Flip_Flop _0 (.J(in_1[0]), .clk(clock_1_out), .K(or_1_out), .Q(_0_q));  // open: Qn, preset, en, reset
  // Probe on _0_q
  J_K_Flip_Flop _1 (.J(or_2_out), .clk(clock_1_out), .K(in_1[0]), .Q(_1_q));  // open: Qn, preset, en, reset
  // Probe on _1_q
  S S (.Q0(_0_q), .Q1(_1_q), .E0(in_1[0]), .E1(in_1[1]), .S0(cambio), .S1(producto));

  assign E0 = in_1[0];
  assign E1 = in_1[1];
endmodule

module q1 (
  input  Q0,
  input  Q1,
  input  E1,
  input  E0,
  output q1_2
);

  wire and_1_out, and_2_out, and_3_out, not_1_out, not_2_out, not_3_out, not_4_out;

  not not_1 (not_1_out, Q0);
  not not_2 (not_2_out, E1);
  not not_3 (not_3_out, Q1);
  and and_1 (and_1_out, not_3_out, E1);
  and and_2 (and_2_out, not_1_out, Q1, not_2_out, E0);
  and and_3 (and_3_out, Q0, not_4_out);
  not not_4 (not_4_out, E0);
  or or_1 (q1_2, and_1_out, and_2_out, and_3_out);
endmodule

module q0 (
  input  Q0,
  input  Q1,
  input  E1,
  input  E0,
  output q0_2
);

  wire and_1_out, and_2_out, and_3_out, not_1_out, not_2_out, not_3_out, not_4_out;

  not not_1 (not_1_out, Q1);
  and and_1 (and_1_out, not_1_out, E0);
  not not_2 (not_2_out, Q0);
  and and_2 (and_2_out, not_2_out, Q1, not_3_out);
  not not_3 (not_3_out, E1);
  and and_3 (and_3_out, Q1, not_4_out);
  not not_4 (not_4_out, E0);
  or or_1 (q0_2, and_1_out, and_2_out, and_3_out);
endmodule

module S (
  input  Q0,
  input  Q1,
  input  E0,
  input  E1,
  output S0,
  output S1
);

  wire and_2_out, and_3_out;

  and and_1 (S0, Q1, E1);
  and and_2 (and_2_out, Q0, E1);
  and and_3 (and_3_out, E0, Q1);
  or or_1 (S1, and_2_out, and_3_out);
endmodule
