// Logisim project ejer1.circ as structural Verilog: 2 circuits, main circuit con puertas basicas
module con_puertas_basicas (
  input  a,
  input  b,
  output s
);

  wire and_1_out, and_2_out, not_1_out, not_2_out;

  not not_1 (not_1_out, a);
  not not_2 (not_2_out, b);
  and and_1 (and_1_out, a, b);
  and and_2 (and_2_out, not_1_out, not_2_out);
  or or_1 (s, and_1_out, and_2_out);
endmodule

module con_exclusiva (
  input  in_1,
  input  in_2,
  output out_3
);

  xnor xnor_1 (out_3, in_1, in_2);
endmodule
