// Logisim project ejer2.circ as structural Verilog: 2 circuits, main circuit original
module original (
  input  a,
  input  b,
  input  c,
  input  d,
  output s
);

  wire and_1_out, nand_1_out, nor_1_out, not_1_out, not_2_out, or_1_out, or_2_out;

  nor nor_1 (nor_1_out, b, d);
  not not_1 (not_1_out, b);
  or or_1 (or_1_out, c, nor_1_out);
  and and_1 (and_1_out, a, not_1_out, or_1_out);
  nand nand_1 (nand_1_out, a, b);
  or or_2 (or_2_out, and_1_out, nand_1_out);
  and and_2 (s, or_2_out, c, not_2_out);
  not not_2 (not_2_out, d);
endmodule

module simplificacion (
  input  a,
  input  b,
  input  c,
  input  d,
  output s
);

  wire and_1_out, and_2_out, not_1_out, not_2_out, not_3_out, not_4_out;

  not not_1 (not_1_out, a);
  and and_1 (and_1_out, not_1_out, c, not_2_out);
  not not_2 (not_2_out, d);
  not not_3 (not_3_out, b);
  and and_2 (and_2_out, not_3_out, c, not_4_out);
  not not_4 (not_4_out, d);
  or or_1 (s, and_1_out, and_2_out);
  original original_1 ();  // open: a, b, c, d, s
endmodule
