// Logisim project ejer4.circ as structural Verilog: 2 circuits, main circuit circuito normal
module circuito_normal (
  input  a,
  input  b,
  input  c,
  input  d,
  output s
);

  wire and_1_out, and_2_out, and_3_out, and_4_out, and_5_out, not_1_out, not_2_out, not_3_out, not_4_out,
       not_5_out, not_6_out, not_7_out, not_8_out;

  not not_1 (not_1_out, a);
  not not_2 (not_2_out, b);
  not not_3 (not_3_out, c);
  not not_4 (not_4_out, a);
  not not_5 (not_5_out, d);
  not not_6 (not_6_out, b);
  not not_7 (not_7_out, d);
  not not_8 (not_8_out, c);
  and and_1 (and_1_out, not_1_out, not_2_out, not_3_out, d);
  and and_2 (and_2_out, not_4_out, c, not_5_out);
  and and_3 (and_3_out, b, c, d);
  and and_4 (and_4_out, a, not_6_out, not_7_out);
  and and_5 (and_5_out, a, b, not_8_out);
  or or_1 (s, and_1_out, and_2_out, and_3_out, and_4_out, and_5_out);
endmodule

module NAND (
  input  a,
  input  b,
  input  c,
  input  d,
  output s
);

  wire nand_1_out, nand_2_out, nand_3_out, nand_4_out, nand_5_out, nand_6_out, nand_7_out, nand_8_out,
       nand_9_out, nand_10_out, nand_11_out, nand_12_out, nand_13_out;

  nand nand_1 (nand_1_out, a, a);
  nand nand_2 (nand_2_out, b, b);
  nand nand_3 (nand_3_out, c, c);
  nand nand_4 (nand_4_out, a, a);
  nand nand_5 (nand_5_out, d, d);
  nand nand_6 (nand_6_out, b, b);
  nand nand_7 (nand_7_out, d, d);
  nand nand_8 (nand_8_out, c, c);
  nand nand_9 (nand_9_out, nand_1_out, nand_2_out, nand_3_out, d);
  nand nand_10 (nand_10_out, nand_4_out, c, nand_5_out);
  nand nand_11 (nand_11_out, b, c, d);
  nand nand_12 (nand_12_out, a, nand_6_out, nand_7_out);
  nand nand_13 (nand_13_out, a, b, nand_8_out);
  nand nand_14 (s, nand_9_out, nand_10_out, nand_11_out, nand_12_out, nand_13_out);
endmodule
