// Logisim project ejer2.circ as structural Verilog: 1 circuit, main circuit main
module main (
  input  [3:0] in_1,
  input  [3:0] in_2,
  input  in_3,
  output [3:0] out_4,
  output out_5
);

  wire adder_1_cout, adder_2_cout, adder_3_cout, xor_1_out, xor_2_out, xor_3_out, xor_4_out;

  xor xor_1 (xor_1_out, in_2[3], in_3);
  xor xor_2 (xor_2_out, in_2[2], in_3);
  xor xor_3 (xor_3_out, in_2[1], in_3);
  xor xor_4 (xor_4_out, in_2[0], in_3);
  Adder #(.width(1)) adder_1 (.a(in_1[0]), .b(xor_4_out), .out(out_4[0]), .cin(in_3), .cout(adder_1_cout));
  Adder #(.width(1)) adder_2 (.a(in_1[1]), .b(xor_3_out), .out(out_4[1]), .cin(adder_1_cout), .cout(adder_2_cout));
  Adder #(.width(1)) adder_3 (.a(in_1[2]), .b(xor_2_out), .out(out_4[2]), .cin(adder_2_cout), .cout(adder_3_cout));
  Adder #(.width(1)) adder_4 (.a(in_1[3]), .b(xor_1_out), .out(out_4[3]), .cin(adder_3_cout), .cout(out_5));
endmodule
