// Logisim project ejer3.circ as structural Verilog: 1 circuit, main circuit main
module main (
  input  B0,
  input  B1,
  input  B2,
  input  B3,
  input  A0,
  input  A1,
  output S0,
  output S1,
  output S2,
  output S3,
  output S4,
  output S5
);

  wire adder_1_cout, adder_2_cout, adder_3_cout, and_1_out, and_2_out, and_3_out, and_4_out, and_5_out,
       and_6_out, and_7_out;

  and and_1 (and_1_out, B1, A0);
  and and_2 (and_2_out, B0, A1);
  and and_3 (and_3_out, B2, A0);
  and and_4 (and_4_out, B1, A1);
  and and_5 (and_5_out, B3, A0);
  and and_6 (and_6_out, B2, A1);
  and and_7 (and_7_out, B3, A1);
  and and_8 (S0, B0, A0);
  Adder #(.width(1)) adder_1 (.a(and_1_out), .b(and_2_out), .out(S1), .cin(1'b0), .cout(adder_1_cout));
  Adder #(.width(1)) adder_2 (.a(and_3_out), .b(and_4_out), .out(S2), .cin(adder_1_cout), .cout(adder_2_cout));
  Adder #(.width(1)) adder_3 (.a(and_5_out), .b(and_6_out), .out(S3), .cin(adder_2_cout), .cout(adder_3_cout));
  Adder #(.width(1)) adder_4 (.a(and_7_out), .b(1'b0), .out(S4), .cin(adder_3_cout), .cout(S5));
endmodule
