// Logisim project ejer5.circ as structural Verilog: 1 circuit, main circuit main
module main (
  input  E,
  input  D,
  input  C,
  input  B,
  input  A
);

  wire multiplexer_1_out, not_1_out;

  not not_1 (not_1_out, 1'b0);
  Multiplexer #(.select(5), .enable("false")) multiplexer_1 (
    .in0(1'b0), .in1(1'b0), .in2(1'b0), .in3(1'b0), .in4(1'b0), .in5(1'b0), .in6(1'b0), .in7(1'b0),
    .in8(1'b0), .in9(not_1_out), .in10(1'b0), .in11(not_1_out), .in12(1'b0), .in13(not_1_out),
    .in14(not_1_out), .in15(not_1_out), .in16(1'b0), .in17(1'b0), .in18(1'b0), .in19(not_1_out), .in20(1'b0),
    .in21(not_1_out), .in22(1'b0), .in23(not_1_out), .in24(not_1_out), .in25(not_1_out), .in26(not_1_out),
    .in27(not_1_out), .in28(not_1_out), .in29(not_1_out), .in30(not_1_out), .in31(not_1_out),
    .out(multiplexer_1_out), .sel({E, D, C, B, A}));
  LED led_1 (.in(multiplexer_1_out));
endmodule
