// Logisim project ejer2.circ as structural Verilog: 1 circuit, main circuit main
module main (
  input  R,
  input  P,
  input  S,
  input  C,
  output Q,
  output nQ
);

  wire clock_1_out, nand_1_out, nand_2_out, nand_3_out, nand_4_out, not_1_out, not_2_out;

  Clock clock_1 (.out(clock_1_out));
  nand nand_1 (nand_1_out, R, clock_1_out);
  nand nand_2 (nand_2_out, nand_1_out, nQ);
  nand nand_3 (nand_3_out, Q, nand_4_out);
  nand nand_4 (nand_4_out, clock_1_out, S);
  not not_1 (not_1_out, P);
  not not_2 (not_2_out, C);
  and and_1 (Q, not_1_out, nand_2_out);
  and and_2 (nQ, nand_3_out, not_2_out);
endmodule
