// Logisim project ejer3.circ as structural Verilog: 2 circuits, main circuit suma de productos
module suma_de_productos (
  input  a,
  input  b,
  input  c,
  input  d,
  output s
);

  wire and_1_out, and_2_out, not_1_out, not_2_out, not_3_out, not_4_out;

  not not_1 (not_1_out, a);
  not not_2 (not_2_out, d);
  not not_3 (not_3_out, b);
  not not_4 (not_4_out, d);
  and and_1 (and_1_out, not_1_out, c, not_2_out);
  and and_2 (and_2_out, not_3_out, c, not_4_out);
  or or_1 (s, and_1_out, and_2_out);
endmodule

module productos_de_sumas (
  input  a,
  input  b,
  input  c,
  input  d,
  output s
);

  wire not_1_out, not_2_out, not_3_out, not_4_out, not_5_out, or_1_out, or_2_out, or_3_out, or_4_out,
       or_5_out;

  not not_1 (not_1_out, b);
  not not_2 (not_2_out, a);
  not not_3 (not_3_out, a);
  not not_4 (not_4_out, a);
  not not_5 (not_5_out, b);
  or or_1 (or_1_out, c, d);
  or or_2 (or_2_out, not_1_out, c);
  or or_3 (or_3_out, not_2_out, c);
  or or_4 (or_4_out, not_3_out, d);
  or or_5 (or_5_out, not_4_out, not_5_out);
  and and_1 (s, or_1_out, or_2_out, or_3_out, or_4_out, or_5_out);
endmodule
